// Logisim project 2.1.circ as structural Verilog: 1 circuit, main circuit main
module main (
  input  [1:0] in_1,
  input  [2:0] in_2,
  output out_3,
  output out_4,
  output out_5,
  output out_6
);

  wire decoder_2_out0, decoder_2_out1, decoder_2_out2, decoder_2_out3, decoder_2_out4, decoder_2_out5,
       decoder_2_out6;

  Decoder #(.select(2), .enable("false")) decoder_1 (
    .out0(out_3), .out1(out_4), .out2(out_5), .out3(out_6), .sel(in_1));
  Decoder #(.select(3), .enable("false")) decoder_2 (
    .out0(decoder_2_out0), .out1(decoder_2_out1), .out2(decoder_2_out2), .out3(decoder_2_out3),
    .out4(decoder_2_out4), .out5(decoder_2_out5), .out6(decoder_2_out6), .sel(in_2));  // open: out7
  // OR_Gate or_1 has open pins: in0=decoder_2_out0, in1=decoder_2_out3, in2=decoder_2_out6, out=open
  // OR_Gate or_2 has open pins: in0=decoder_2_out0, in1=decoder_2_out3, in2=decoder_2_out4, in3=decoder_2_out6, out=open
  // OR_Gate or_3 has open pins: in0=decoder_2_out0, in1=decoder_2_out1, in2=decoder_2_out2, in3=decoder_2_out3, in4=decoder_2_out4, in5=decoder_2_out5, in6=decoder_2_out6, out=open

  // Notes on the sheet:
  //   F1
  //   F2
  //   F3
endmodule
