// Logisim project 2.3.circ as structural Verilog: 1 circuit, main circuit main
module main (
  input  C,
  input  in_2,
  input  [1:0] AB,
  input  in_4,
  input  in_5,
  input  [2:0] ABC,
  output out_7,
  output out_8
);

  wire not_1_out, not_2_out;
  wire [2:0] undriven;

  Multiplexer #(.select(3), .enable("false")) multiplexer_1 (
    .in0(in_5), .in1(in_4), .in2(in_4), .in3(in_5), .in4(in_4), .in5(in_4), .in6(in_5), .in7(in_4),
    .out(out_8), .sel(undriven));
  not not_1 (not_1_out, C);
  not not_2 (not_2_out, C);
  Multiplexer #(.select(2), .enable("false")) multiplexer_2 (
    .in0(not_1_out), .in1(C), .in2(in_2), .in3(not_2_out), .out(out_7), .sel(AB));
endmodule
