// Logisim project 4.circ as structural Verilog: 3 circuits, main circuit main
module main (
  input  [3:0] A,
  input  [3:0] B,
  output [4:0] Output
);

  wire FA1_cout, FA2_cout, HA1_c;

  Full_Adder FA3 (.A(A[3]), .B(B[3]), .Cin(FA2_cout), .Cout(Output[4]), .S(Output[3]));
  Full_Adder FA2 (.A(A[2]), .B(B[2]), .Cin(FA1_cout), .Cout(FA2_cout), .S(Output[2]));
  Full_Adder FA1 (.A(A[1]), .B(B[1]), .Cin(HA1_c), .Cout(FA1_cout), .S(Output[1]));
  Half_Adder HA1 (.A(A[0]), .B(B[0]), .C(HA1_c), .S(Output[0]));
endmodule

module Half_Adder (
  input  A,
  input  B,
  output C,
  output S
);

  and and_1 (C, A, B);
  xor xor_1 (S, B, A);
endmodule

module Full_Adder (
  input  A,
  input  B,
  input  Cin,
  output Cout,
  output S
);

  wire and_1_out, and_2_out, and_3_out, xor_1_out;

  and and_1 (and_1_out, A, B);
  and and_2 (and_2_out, A, Cin);
  and and_3 (and_3_out, B, Cin);
  xor xor_1 (xor_1_out, A, Cin);
  xor xor_2 (S, xor_1_out, B);
  or or_1 (Cout, and_1_out, and_2_out, and_3_out);
endmodule
