// Logisim project Lab 3.circ as structural Verilog: 2 circuits, main circuit main
module main (
  input  Load,
  input  in_2,
  input  [3:0] Input_D,
  input  [3:0] in_4,
  input  _100110111,
  input  i0,
  input  Id,
  input  shr,
  input  i1,
  input  shl,
  input  i2,
  input  shl_in,
  input  shr_in,
  input  i3,
  output Output_Q,
  output out_16,
  output [3:0] Output_Q_2,
  output Q0,
  output Q1,
  output Q2,
  output Q3
);

  wire clock_1_out, clock_2_out, clock_3_out, clock_4_out, FF0_3_q, FF0_q, FF1_3_q, FF1_q, FF2_4_q, FF2_q,
       multiplexer_1_out, multiplexer_2_out, multiplexer_3_out, multiplexer_4_out, multiplexer_5_out,
       multiplexer_6_out, multiplexer_7_out, multiplexer_8_out, undriven, undriven_2;
  wire [1:0] combinational_logic_1_s1;

  Clock clock_1 (.out(clock_1_out));
  D_Flip_Flop FF0 (.clk(clock_1_out), .D(_100110111), .Q(FF0_q));  // open: Qn, preset, en, reset
  D_Flip_Flop FF1 (.clk(clock_1_out), .D(FF0_q), .Q(FF1_q));  // open: Qn, preset, en, reset
  D_Flip_Flop FF2 (.clk(clock_1_out), .D(FF1_q), .Q(FF2_q));  // open: Qn, preset, en, reset
  Combinational_Logic combinational_logic_1 (
    .Id(Id), .shr(shr), .shl(shl), .S1(combinational_logic_1_s1[0]), .S2(combinational_logic_1_s1[1]));
  D_Flip_Flop FF3 (.clk(clock_1_out), .D(FF2_q), .Q(out_16));  // open: Qn, preset, en, reset
  Clock clock_2 (.out(clock_2_out));
  Clock clock_3 (.out(clock_3_out));
  Multiplexer #(.select(2), .enable("false")) multiplexer_1 (
    .in0(Q0), .in1(shl_in), .in2(undriven_2), .in3(i0), .out(multiplexer_1_out),
    .sel(combinational_logic_1_s1));
  Multiplexer #(.select(2), .enable("false")) multiplexer_2 (
    .in0(Q1), .in1(Q0), .in2(undriven), .in3(i1), .out(multiplexer_2_out), .sel(combinational_logic_1_s1));
  Multiplexer #(.select(2), .enable("false")) multiplexer_3 (
    .in0(Q2), .in1(undriven_2), .in2(Q3), .in3(i2), .out(multiplexer_3_out), .sel(combinational_logic_1_s1));
  Multiplexer #(.select(2), .enable("false")) multiplexer_4 (
    .in0(Q3), .in1(undriven), .in2(shr_in), .in3(i3), .out(multiplexer_4_out), .sel(combinational_logic_1_s1));
  Multiplexer #(.enable("false")) multiplexer_5 (.in0(in_2), .in1(Input_D[0]), .out(multiplexer_5_out), .sel(Load));
  D_Flip_Flop FF0_2 (.clk(clock_3_out), .D(multiplexer_1_out), .Q(Q0));  // open: Qn, preset, en, reset
  D_Flip_Flop FF1_2 (.clk(clock_3_out), .D(multiplexer_2_out), .Q(Q1));  // open: Qn, preset, en, reset
  D_Flip_Flop FF2_2 (.clk(clock_3_out), .D(multiplexer_3_out), .Q(Q2));  // open: Qn, preset, en, reset
  D_Flip_Flop FF3_2 (.clk(clock_3_out), .D(multiplexer_4_out), .Q(Q3));  // open: Qn, preset, en, reset
  D_Flip_Flop FF0_3 (.clk(clock_2_out), .D(multiplexer_5_out), .Q(FF0_3_q));  // open: Qn, preset, en, reset
  Clock clock_4 (.out(clock_4_out));
  Multiplexer #(.enable("false")) multiplexer_6 (.in0(FF0_3_q), .in1(Input_D[1]), .out(multiplexer_6_out), .sel(Load));
  D_Flip_Flop FF0_4 (.clk(clock_4_out), .D(in_4[0]), .Q(Output_Q_2[0]));  // open: Qn, preset, en, reset
  D_Flip_Flop FF1_3 (.clk(clock_2_out), .D(multiplexer_6_out), .Q(FF1_3_q));  // open: Qn, preset, en, reset
  D_Flip_Flop FF1_4 (.clk(clock_4_out), .D(in_4[1]), .Q(Output_Q_2[1]));  // open: Qn, preset, en, reset
  Multiplexer #(.enable("false")) multiplexer_7 (.in0(FF1_3_q), .in1(Input_D[2]), .out(multiplexer_7_out), .sel(Load));
  D_Flip_Flop FF2_3 (.clk(clock_4_out), .D(in_4[2]), .Q(Output_Q_2[2]));  // open: Qn, preset, en, reset
  D_Flip_Flop FF2_4 (.clk(clock_2_out), .D(multiplexer_7_out), .Q(FF2_4_q));  // open: Qn, preset, en, reset
  Multiplexer #(.enable("false")) multiplexer_8 (.in0(FF2_4_q), .in1(Input_D[3]), .out(multiplexer_8_out), .sel(Load));
  D_Flip_Flop FF3_3 (.clk(clock_4_out), .D(in_4[3]), .Q(Output_Q_2[3]));  // open: Qn, preset, en, reset
  D_Flip_Flop FF2_5 (.clk(clock_2_out), .D(multiplexer_8_out), .Q(Output_Q));  // open: Qn, preset, en, reset

  // Notes on the sheet:
  //   0001 0010 0100 1001 0011 0110 1101  1011 0111 
  //   Q0
  //   Q1
  //   Q2
  //   Q3
endmodule

module Combinational_Logic (
  input  Id,
  input  shr,
  input  shl,
  output S1,
  output S2
);

  wire and_1_out, and_2_out, not_1_out;

  not not_1 (not_1_out, shr);
  and and_1 (and_1_out, Id, not_1_out);
  and and_2 (and_2_out, not_1_out, shl);
  or or_1 (S1, and_1_out, shr);
  or or_2 (S2, Id, and_2_out);
endmodule
