// Logisim project lab3.4.circ as structural Verilog: 1 circuit, main circuit main
module main (
  input  [3:0] I3_I2_I1_I0,
  output [3:0] Q3_Q2_Q1_Q0
);

  wire clk_out;

  Clock clk (.out(clk_out));
  D_Flip_Flop d_ff_1 (.clk(clk_out), .D(I3_I2_I1_I0[0]), .Q(Q3_Q2_Q1_Q0[0]));  // open: Qn, preset, en, reset
  D_Flip_Flop d_ff_2 (.clk(clk_out), .D(I3_I2_I1_I0[1]), .Q(Q3_Q2_Q1_Q0[1]));  // open: Qn, preset, en, reset
  D_Flip_Flop d_ff_3 (.clk(clk_out), .D(I3_I2_I1_I0[2]), .Q(Q3_Q2_Q1_Q0[2]));  // open: Qn, preset, en, reset
  D_Flip_Flop d_ff_4 (.clk(clk_out), .D(I3_I2_I1_I0[3]), .Q(Q3_Q2_Q1_Q0[3]));  // open: Qn, preset, en, reset

  // Notes on the sheet:
  //   PIPO
endmodule
