// Logisim project lab5.circ as structural Verilog: 3 circuits, main circuit main
module main (
  input  [7:0] Input_A,
  input  [7:0] Input_B,
  input  Enable,
  input  [2:0] Select
);

  wire n7segdecoder_1_a, n7segdecoder_1_b, n7segdecoder_1_c, n7segdecoder_1_d, n7segdecoder_1_e,
       n7segdecoder_1_f, n7segdecoder_1_g, n7segdecoder_2_a, n7segdecoder_2_b, n7segdecoder_2_c,
       n7segdecoder_2_d, n7segdecoder_2_e, n7segdecoder_2_f, n7segdecoder_2_g, n7segdecoder_3_a,
       n7segdecoder_3_b, n7segdecoder_3_c, n7segdecoder_3_d, n7segdecoder_3_e, n7segdecoder_3_f,
       n7segdecoder_3_g;
  wire [7:0] alu_1_out_5, divider_1_out, divider_2_out, divider_3_rem, divider_4_rem, divider_5_rem;

  ALU alu_1 (.Input_A(Input_A), .Input_B(Input_B), .Select(Select), .Enable(Enable), .out_5(alu_1_out_5));
  Divider divider_1 (.a(alu_1_out_5), .b(8'h64), .out(divider_1_out));  // open: upper, rem
  Divider divider_2 (.a(alu_1_out_5), .b(8'ha), .out(divider_2_out));  // open: upper, rem
  Divider divider_3 (.a(alu_1_out_5), .b(8'ha), .rem(divider_3_rem));  // open: out, upper
  Divider divider_4 (.a(divider_1_out), .b(8'ha), .rem(divider_4_rem));  // open: out, upper
  Divider divider_5 (.a(divider_2_out), .b(8'ha), .rem(divider_5_rem));  // open: out, upper
  _7segdecoder u_7segdecoder_1 (
    .in_1(divider_4_rem), .a(n7segdecoder_1_a), .b(n7segdecoder_1_b), .c(n7segdecoder_1_c),
    .d(n7segdecoder_1_d), .e(n7segdecoder_1_e), .f(n7segdecoder_1_f), .g(n7segdecoder_1_g));
  _7segdecoder u_7segdecoder_2 (
    .in_1(divider_5_rem), .a(n7segdecoder_2_a), .b(n7segdecoder_2_b), .c(n7segdecoder_2_c),
    .d(n7segdecoder_2_d), .e(n7segdecoder_2_e), .f(n7segdecoder_2_f), .g(n7segdecoder_2_g));
  _7segdecoder u_7segdecoder_3 (
    .in_1(divider_3_rem), .a(n7segdecoder_3_a), .b(n7segdecoder_3_b), .c(n7segdecoder_3_c),
    .d(n7segdecoder_3_d), .e(n7segdecoder_3_e), .f(n7segdecoder_3_f), .g(n7segdecoder_3_g));
  _7_Segment_Display u_7_segment_display_1 (
    .g(n7segdecoder_1_a), .f(n7segdecoder_1_b), .a(n7segdecoder_1_c), .b(n7segdecoder_1_d),
    .e(n7segdecoder_1_e), .d(n7segdecoder_1_f), .c(n7segdecoder_1_g));  // open: dp
  _7_Segment_Display u_7_segment_display_2 (
    .g(n7segdecoder_2_a), .f(n7segdecoder_2_b), .a(n7segdecoder_2_c), .b(n7segdecoder_2_d),
    .e(n7segdecoder_2_e), .d(n7segdecoder_2_f), .c(n7segdecoder_2_g));  // open: dp
  _7_Segment_Display u_7_segment_display_3 (
    .g(n7segdecoder_3_a), .f(n7segdecoder_3_b), .a(n7segdecoder_3_c), .b(n7segdecoder_3_d),
    .e(n7segdecoder_3_e), .d(n7segdecoder_3_f), .c(n7segdecoder_3_g));  // open: dp

  // Notes on the sheet:
  //   Hundreds
  //   Tens
  //   Units
  //   7seg1
  //   7seg2
  //   7seg3
endmodule

module _7segdecoder (
  input  [7:0] in_1,
  output a,
  output b,
  output c,
  output d,
  output e,
  output f,
  output g
);

  wire [7:7] multiplexer_1_out;

  Multiplexer #(.select(4), .width(8), .enable("false")) multiplexer_1 (
    .in0(8'h7e), .in1(8'h48), .in2(8'h3d), .in3(8'h6d), .in4(8'h4b), .in5(8'h67), .in6(8'h77), .in7(8'h4c),
    .in8(8'h7f), .in9(8'h6f), .in10(8'h37), .in11(8'h37), .in12(8'h37), .in13(8'h37), .in14(8'h37),
    .in15(8'h37), .out({multiplexer_1_out[7], g, f, e, d, c, b, a}), .sel(in_1[3:0]));

  // Notes on the sheet:
  //   0
  //   1
  //   2
  //   3
  //   4
  //   5
  //   6
  //   7
  //   8
  //   9
  //   E
endmodule

module ALU (
  input  [7:0] Input_A,
  input  [7:0] Input_B,
  input  [2:0] Select,
  input  Enable,
  output [7:0] out_5
);

  wire comparator_1_gt;
  wire [7:0] adder_1_out, and_1_out, divider_1_out, multiplexer_1_out, multiplier_1_out, shifter_1_out,
       shifter_2_out, subtractor_1_out;

  Adder adder_1 (.a(Input_A), .b(Input_B), .out(adder_1_out));  // open: cin, cout
  Subtractor subtractor_1 (.a(Input_A), .b(Input_B), .out(subtractor_1_out));  // open: bin, bout
  Multiplier multiplier_1 (.a(Input_A), .b(Input_B), .out(multiplier_1_out));  // open: cin, cout
  Divider divider_1 (.a(Input_A), .b(Input_B), .out(divider_1_out));  // open: upper, rem
  assign and_1_out = Input_A & Input_B;  // AND_Gate and_1, 8 bits wide
  Shifter shifter_1 (.in(Input_B), .\dist (3'b001), .out(shifter_1_out));
  Shifter #(.shift("lr")) shifter_2 (.in(Input_A), .\dist (3'b010), .out(shifter_2_out));
  Comparator comparator_1 (.a(Input_A), .b(Input_B), .gt(comparator_1_gt));  // open: eq, lt
  Multiplexer #(.width(8), .enable("false")) multiplexer_1 (
    .in0(Input_B), .in1(Input_A), .out(multiplexer_1_out), .sel(comparator_1_gt));
  Multiplexer #(.select(3), .width(8)) multiplexer_2 (
    .in0(adder_1_out), .in1(subtractor_1_out), .in2(multiplier_1_out), .in3(divider_1_out), .in4(and_1_out),
    .in5(shifter_1_out), .in6(shifter_2_out), .in7(multiplexer_1_out), .out(out_5), .sel(Select), .en(Enable));

  // Notes on the sheet:
  //   Adder
  //   Subtractor
  //   Multiplier
  //   Divider
  //   Bitwise AND
  //   Shift input B Left by 1 bit
  //   Shift input A right by 2 bits
  //   Max number
endmodule
