// Logisim project 2.2.circ as structural Verilog: 1 circuit, main circuit main
module main (
  input  A,
  input  B,
  input  [1:0] in_3,
  output [1:0] out_4
);

  wire [1:0] and_1_out, or_1_out, xnor_1_out, xor_1_out;

  and and_1 (and_1_out[0], A, B);
  or or_1 (or_1_out[0], A, B);
  xor xor_1 (xor_1_out[0], A, B);
  xnor xnor_1 (xnor_1_out[0], A, B);
  Multiplexer #(.select(2), .width(2), .enable("false")) multiplexer_1 (
    .in0(and_1_out), .in1(or_1_out), .in2(xor_1_out), .in3(xnor_1_out), .out(out_4), .sel(in_3));
  // Pins of 1 and 2 bits meet at and_1_out
  // Pins of 1 and 2 bits meet at or_1_out
  // Pins of 1 and 2 bits meet at xor_1_out
  // Pins of 1 and 2 bits meet at xnor_1_out
endmodule
