// Logisim project 3.2.circ as structural Verilog: 1 circuit, main circuit main
module main (
  input  [3:0] in_1,
  input  in_2,
  output out_3
);

  wire clock_1_out, d_ff_1_q, d_ff_2_q, d_ff_3_q, nand_1_out, nand_2_out, nand_3_out, nand_4_out, nand_5_out,
       nand_6_out, nand_7_out, nand_8_out, nand_9_out, not_1_out;

  Clock clock_1 (.out(clock_1_out));
  not not_1 (not_1_out, in_2);
  D_Flip_Flop d_ff_1 (.clk(clock_1_out), .D(in_1[0]), .Q(d_ff_1_q));  // open: Qn, preset, en, reset
  nand nand_1 (nand_1_out, in_1[1], not_1_out);
  nand nand_2 (nand_2_out, in_2, d_ff_1_q);
  nand nand_3 (nand_3_out, nand_1_out, nand_2_out);
  nand nand_4 (nand_4_out, in_1[2], not_1_out);
  nand nand_5 (nand_5_out, in_2, d_ff_2_q);
  D_Flip_Flop d_ff_2 (.clk(clock_1_out), .D(nand_3_out), .Q(d_ff_2_q));  // open: Qn, preset, en, reset
  nand nand_6 (nand_6_out, nand_4_out, nand_5_out);
  D_Flip_Flop d_ff_3 (.clk(clock_1_out), .D(nand_6_out), .Q(d_ff_3_q));  // open: Qn, preset, en, reset
  nand nand_7 (nand_7_out, in_1[3], not_1_out);
  nand nand_8 (nand_8_out, in_2, d_ff_3_q);
  nand nand_9 (nand_9_out, nand_7_out, nand_8_out);
  D_Flip_Flop d_ff_4 (.clk(clock_1_out), .D(nand_9_out), .Q(out_3));  // open: Qn, preset, en, reset

  // Notes on the sheet:
  //   PISO
endmodule
