// Logisim project 3.3.circ as structural Verilog: 2 circuits, main circuit main
module main (
  input  shl_in,
  input  I0,
  input  I1,
  input  I2,
  input  I3,
  input  shr_in,
  input  Id,
  input  shr,
  input  shl,
  output Q0,
  output Q1,
  output Q2,
  output Q3
);

  wire clock_1_out, multiplexer_1_out, multiplexer_2_out, multiplexer_3_out, multiplexer_4_out;
  wire [1:0] combinational_logic_1_s0;

  Combinational_Logic combinational_logic_1 (
    .Id(Id), .shr(shr), .shl(shl), .S1(combinational_logic_1_s0[1]), .S0(combinational_logic_1_s0[0]));
  Clock clock_1 (.out(clock_1_out));
  Multiplexer #(.select(2), .enable("false")) multiplexer_1 (
    .in0(Q0), .in1(I0), .in2(Q1), .in3(shl_in), .out(multiplexer_1_out), .sel(combinational_logic_1_s0));
  Multiplexer #(.select(2), .enable("false")) multiplexer_2 (
    .in0(Q1), .in1(I1), .in2(Q2), .in3(Q0), .out(multiplexer_2_out), .sel(combinational_logic_1_s0));
  Multiplexer #(.select(2), .enable("false")) multiplexer_3 (
    .in0(Q2), .in1(I2), .in2(Q3), .in3(Q1), .out(multiplexer_3_out), .sel(combinational_logic_1_s0));
  Multiplexer #(.select(2), .enable("false")) multiplexer_4 (
    .in0(Q3), .in1(I3), .in2(shr_in), .in3(Q2), .out(multiplexer_4_out), .sel(combinational_logic_1_s0));
  D_Flip_Flop d_ff_1 (.clk(clock_1_out), .D(multiplexer_1_out), .Q(Q0));  // open: Qn, preset, en, reset
  D_Flip_Flop d_ff_2 (.clk(clock_1_out), .D(multiplexer_2_out), .Q(Q1));  // open: Qn, preset, en, reset
  D_Flip_Flop d_ff_3 (.clk(clock_1_out), .D(multiplexer_3_out), .Q(Q2));  // open: Qn, preset, en, reset
  D_Flip_Flop d_ff_4 (.clk(clock_1_out), .D(multiplexer_4_out), .Q(Q3));  // open: Qn, preset, en, reset
endmodule

module Combinational_Logic (
  input  Id,
  input  shr,
  input  shl,
  output S1,
  output S0
);

  wire and_1_out, and_2_out, and_3_out, not_1_out, not_2_out, not_3_out;

  not not_1 (not_1_out, Id);
  not not_2 (not_2_out, Id);
  not not_3 (not_3_out, shr);
  and and_1 (and_1_out, not_1_out, shl);
  and and_2 (and_2_out, not_2_out, shr);
  and and_3 (and_3_out, not_3_out, shl);
  or or_1 (S1, and_1_out, and_2_out);
  or or_2 (S0, and_3_out, Id);
endmodule
