// Logisim project useful.circ as structural Verilog: 1 circuit, main circuit main
module main (
  input  A,
  input  B,
  input  C,
  input  D,
  output Z
);

  wire and_1_out, and_2_out, not_1_out, not_2_out, not_3_out;

  not not_1 (not_1_out, A);
  not not_2 (not_2_out, B);
  and and_1 (and_1_out, not_2_out, C, D);
  and and_2 (and_2_out, B, not_3_out);
  not not_3 (not_3_out, D);
  or or_1 (Z, not_1_out, and_1_out, and_2_out);
endmodule
